# Fritzing sketch Ipass_Sketch_RX (saved by Fritzing 0.9.6b)
breadboards: 1

parts:
  RF24L01 = NRF24L01
  RGB_SMD_LED1 = APA102-2020 [package=2020]
  RGB_SMD_LED2 = APA102-2020 [package=2020]
  RGB_SMD_LED3 = APA102-2020 [package=2020]
  RGB_SMD_LED4 = APA102-2020 [package=2020]
  RGB_SMD_LED8 = APA102-2020 [package=2020]
  RGB_SMD_LED6 = APA102-2020 [package=2020]
  RGB_SMD_LED7 = APA102-2020 [package=2020]
  RGB_SMD_LED5 = APA102-2020 [package=2020]
  Onderdeel11 = Arduino Due (Rev2b)
  V1 = DC Power [voltage=3.3V]

nets:
  N1: RF24L01.IRQ, Onderdeel11.D0/RX
  N2: RF24L01.MOSI, Onderdeel11.D2_PWM
  N3: RF24L01.CSN, Onderdeel11.D8_PWM
  N4: RF24L01.VCC, V1.V+
  N5: RF24L01.MISO, Onderdeel11.D4_PWM/SS1
  N6: RF24L01.SCK, Onderdeel11.D3_PWM
  N7: RF24L01.CE, Onderdeel11.D6_PWM
  GND: RF24L01.GND, RGB_SMD_LED1.GND, RGB_SMD_LED2.GND, RGB_SMD_LED3.GND, RGB_SMD_LED4.GND, RGB_SMD_LED8.GND, RGB_SMD_LED6.GND, RGB_SMD_LED7.GND, RGB_SMD_LED5.GND, Onderdeel11.GND, V1.V-
  VCC: RGB_SMD_LED1.VCC, RGB_SMD_LED2.VCC, RGB_SMD_LED3.VCC, RGB_SMD_LED4.VCC, RGB_SMD_LED8.VCC, RGB_SMD_LED6.VCC, RGB_SMD_LED7.VCC, RGB_SMD_LED5.VCC, Onderdeel11.5V
  N8: RGB_SMD_LED1.CKO, RGB_SMD_LED2.CKI
  N9: RGB_SMD_LED1.SDO, RGB_SMD_LED2.SDI
  N10: RGB_SMD_LED1.SDI, Onderdeel11.D12_PWM
  N11: RGB_SMD_LED1.CKI, Onderdeel11.D13_PWM
  N12: RGB_SMD_LED2.CKO, RGB_SMD_LED3.CKI
  N13: RGB_SMD_LED2.SDO, RGB_SMD_LED3.SDI
  N14: RGB_SMD_LED3.CKO, RGB_SMD_LED4.CKI
  N15: RGB_SMD_LED3.SDO, RGB_SMD_LED4.SDI
  N16: RGB_SMD_LED4.CKO, RGB_SMD_LED5.CKI
  N17: RGB_SMD_LED4.SDO, RGB_SMD_LED5.SDI
  N18: RGB_SMD_LED8.SDI, RGB_SMD_LED7.SDO
  N19: RGB_SMD_LED8.CKI, RGB_SMD_LED7.CKO
  N20: RGB_SMD_LED6.CKO, RGB_SMD_LED7.CKI
  N21: RGB_SMD_LED6.SDO, RGB_SMD_LED7.SDI
  N22: RGB_SMD_LED6.SDI, RGB_SMD_LED5.SDO
  N23: RGB_SMD_LED6.CKI, RGB_SMD_LED5.CKO

custom parts:
  APA102-2020: APA102-2020 2mm x 2mm Individually addressable LED. Note: there are at least 3 and possibly more incompatible footprints for these LEDs from different manufacturers. This particular part is for the APA Electronic Co APA-102-2020 device (data sheet at http://neon-world.com/uploads/wenjian/20apa.pdf). Check the PCB foot print of the device you have before using this part.
