# Fritzing sketch Ipass_Sketch_TX (saved by Fritzing 0.9.6b)
breadboards: 1

parts:
  Arduino_Due = Arduino Due (Rev2b)
  R1 = Rotary Potentiometer (Large) [maximum_resistance=100kΩ package=THT]
  R2 = Rotary Potentiometer (Large) [maximum_resistance=100kΩ package=THT]
  R3 = Rotary Potentiometer (Large) [maximum_resistance=100kΩ package=THT]
  R4 = Rotary Potentiometer (Large) [maximum_resistance=100kΩ package=THT]
  RF24L01 = NRF24L01
  S1 = Pushbutton [package="[THT]"]
  S2 = Pushbutton [package="[THT]"]
  S3 = Pushbutton [package="[THT]"]
  R5 = Resistor [tolerance=±5% power=0.25 resistance=220 package=THT]
  R6 = Resistor [tolerance=±5% power=0.25 resistance=220 package=THT]
  R7 = Resistor [tolerance=±5% power=0.25 resistance=220 package=THT]
  V1 = DC Power [voltage=3.3V frequency=60]

nets:
  N1: Arduino_Due.A8, R2.wiper
  N2: Arduino_Due.A10, R1.wiper
  N3: Arduino_Due.A0, R4.wiper
  N4: Arduino_Due.A6, R3.wiper
  GND: Arduino_Due.GND, R1.leg2, R2.leg2, R3.leg2, R4.leg2, RF24L01.GND, R5.Pin_0, R6.Pin_0, R7.Pin_0, V1.V-
  N5: Arduino_Due.D8_PWM, RF24L01.CSN
  N6: Arduino_Due.D11_PWM, S2.Pin_3, S2.Pin_4, R6.Pin_1
  N7: Arduino_Due.D13_PWM, S3.Pin_3, S3.Pin_4, R5.Pin_1
  N8: Arduino_Due.D0/RX, RF24L01.IRQ
  N9: Arduino_Due.D2_PWM, RF24L01.MOSI
  N10: Arduino_Due.D3_PWM, RF24L01.SCK
  N11: Arduino_Due.D4_PWM/SS1, RF24L01.MISO
  N12: Arduino_Due.D6_PWM, RF24L01.CE
  N13: Arduino_Due.D52, S1.Pin_3, S1.Pin_4, R7.Pin_1
  N14: R1.leg1, R2.leg1, R3.leg1, R4.leg1, RF24L01.VCC, S1.Pin_2, S2.Pin_2, S3.Pin_2, V1.V+
