# Fritzing sketch example_HC_SR04_RX (saved by Fritzing 0.9.6b)
breadboards: 1

parts:
  RF24L01 = NRF24L01
  Arduino_due = Arduino Due (Rev2b)
  V1 = DC Power [voltage=3.3V frequency=60]

nets:
  N1: RF24L01.IRQ, Arduino_due.D0/RX
  N2: RF24L01.MOSI, Arduino_due.D2_PWM
  N3: RF24L01.CSN, Arduino_due.D8_PWM
  N4: RF24L01.VCC, V1.V-
  N5: RF24L01.MISO, Arduino_due.D4_PWM/SS1
  N6: RF24L01.SCK, Arduino_due.D3_PWM
  N7: RF24L01.CE, Arduino_due.D6_PWM
  GND: RF24L01.GND, Arduino_due.GND, V1.V+
