# Fritzing sketch example_HC_SR04_TX (saved by Fritzing 0.9.6b)
breadboards: 1

parts:
  Arduino_due = Arduino Due (Rev2b)
  RF24L01 = NRF24L01
  HC-SR04 = HC-SR04 Ultrasonic Distance Sensor
  R1 = Resistor [tolerance=±5% resistance=1000 package="2512 [SMD]"]
  R2 = Resistor [tolerance=±5% resistance=1000 package="2512 [SMD]"]
  V1 = DC Power [voltage=3.3V frequency=60]

nets:
  N1: Arduino_due.D20/SDA3, HC-SR04.TRIG
  5V: Arduino_due.5V, HC-SR04.VCC
  GND: Arduino_due.GND, RF24L01.GND, HC-SR04.GND, R2.Pin_0, V1.V+
  N2: Arduino_due.D8_PWM, RF24L01.CSN
  N3: Arduino_due.D0/RX, RF24L01.SCK
  N4: Arduino_due.D2_PWM, RF24L01.MOSI
  N5: Arduino_due.D4_PWM/SS1, RF24L01.MISO
  N6: Arduino_due.D6_PWM, RF24L01.CE
  N7: Arduino_due.D22, R1.Pin_0, R2.Pin_1
  N8: RF24L01.VCC, V1.V-
  N9: HC-SR04.ECHO, R1.Pin_1
